# Fritzing sketch Schematic (saved by Fritzing 0.9.6b)

parts:
  HC-SR04_Sensor_1 = HC-SR04 Ultrasonic Distance Sensor
  LED1 = smd LED [color="Red (633nm)" package="0805 [SMD]"]
  Part1 = Arduino Uno (Rev3) - ICSP

nets:
  VCC: HC-SR04_Sensor_1.VCC, Part1.5V
  N1: HC-SR04_Sensor_1.TRIG, Part1.A0
  N2: HC-SR04_Sensor_1.ECHO, Part1.A1
  GND: HC-SR04_Sensor_1.GND, LED1.cathode, Part1.GND
  N3: LED1.anode, Part1.D2
